// Logisim project cpu.circ as structural Verilog: 10 circuits, main circuit main
module main (
);

  wire _4WE, _5WE, aluEq, and_5_out, and_6_out, and_7_out, and_8_out, and_10_out, and_11_out, \break ,
       button_1_out, button_2_out, button_3_out, clk, clock_1_out, comparator_3_eq, comparator_5_eq,
       comparator_6_eq, comparator_8_eq, comparator_9_eq, comparator_10_eq, condjump, cp0, eret,
       interrupt_1__1wait, interrupt_1__2wait, interrupt_1__3wait, jal, jump, lessthan0, load_use, lw, mfc0,
       mtc0, not_1_out, not_2_out, not_3_out, not_4_out, or_1_out, or_5_out, R, register_2_q, select,
       syscall, uncondjump, WE;
  wire [3:0] ALUOP, controller_1_aluop, register_3_q, register_3_q_2, register_3_q_4, register_3_q_5,
       register_3_q_6, register_3_q_7, register_3_q_8;
  wire [4:0] multiplexer_5_out, multiplexer_6_out, multiplexer_7_out, multiplexer_8_out, rd;
  wire [11:8] register_3_q_3;
  wire [15:0] multiplexer_29_out;
  wire [25:4] controller_1_aluy;
  wire [31:0] _4Res, _4RW_num, _5Res, _5RW_num, adder_1_out, adder_2_out, adder_3_out, adder_4_out, alu_1_p5,
       bit_extender_1_out, bit_extender_2_out, bit_extender_3_out, bit_extender_4_out, bit_extender_5_out,
       bit_extender_6_out, bit_extender_7_out, bit_extender_8_out, counter_1_q, counter_2_q, counter_3_q,
       counter_4_q, counter_5_q, cp0Data, intAddr, main_1_p7, main_1_p8, multiplexer_3_out,
       multiplexer_9_out, multiplexer_10_out, multiplexer_11_out, multiplexer_12_out, multiplexer_13_out,
       multiplexer_14_out, multiplexer_15_out, multiplexer_16_out, multiplexer_17_out, multiplexer_18_out,
       multiplexer_19_out, multiplexer_20_out, multiplexer_21_out, multiplexer_22_out, multiplexer_23_out,
       multiplexer_24_out, multiplexer_26_out, multiplexer_28_out, multiplexer_30_out, PC, ram_1_data,
       redirect_1_output, redirect_2_output, regbuf_1_out1, regbuf_1_out2, regbuf_2_out1, regbuf_2_out2,
       regbuf_2_out4, regbuf_2_out5, regbuf_2_out6, regbuf_2_out7, regbuf_2_out8, regbuf_3_out1,
       regbuf_3_out2, regbuf_3_out4, regbuf_3_out6, regbuf_4_out1, regbuf_4_out2, regbuf_4_out3,
       regbuf_4_out4, regbuf_4_out5, regbuf_4_out7, register_1_q, RF_rt, rom_1_data, save, shifter_1_out,
       shifter_2_out, undriven;
  wire [31:4] regbuf_2_out3;

  Multiplexer #(.width(32), .enable("false")) multiplexer_1 (
    .in0(adder_1_out), .in1(multiplexer_9_out), .out(save), .sel(jump));
  Register #(.width(32)) register_1 (.D(save), .en(not_1_out), .Q(register_1_q), .clk(clk));  // open: clr
  not not_1 (not_1_out, load_use);
  // NAND_Gate nand_1 has open pins: in0=\break , in1=eret, out=open
  Multiplexer #(.width(32), .enable("false")) multiplexer_2 (.in1(intAddr), .sel(select));  // open: in0, out
  Button button_1 (.out(button_1_out));
  Button button_2 (.out(button_2_out));
  Button button_3 (.out(button_3_out));
  Multiplexer #(.width(32), .enable("false")) multiplexer_3 (
    .in0(save), .in1(RF_rt), .out(multiplexer_3_out), .sel(mtc0));
  Adder #(.width(32)) adder_1 (.a(32'h4), .b(register_1_q), .out(adder_1_out), .cin(1'b0));  // open: cout
  Multiplexer #(.width(32), .enable("false")) multiplexer_4 (.in1(cp0Data), .sel(eret));  // open: in0, out
  interrupt interrupt_1 (
    .int1(button_1_out), .int2(button_2_out), .int3(button_3_out), .WE(mtc0), .in(multiplexer_3_out),
    .w_num(rd), .clk(clk), ._1wait(interrupt_1__1wait), ._2wait(interrupt_1__2wait), .address(intAddr),
    .\break (\break ), .select(select), ._3wait(interrupt_1__3wait), .eret(eret), .R_num(rd), .out(cp0Data));
  ROM #(.addrWidth(10), .dataWidth(32)) rom_1 (.addr(register_1_q[11:2]), .data(rom_1_data), .sel(1'b1));
  not not_2 (not_2_out, load_use);
  LED _1 (.in(interrupt_1__1wait));
  LED _2 (.in(interrupt_1__2wait));
  LED _3 (.in(interrupt_1__3wait));
  regBuf regbuf_1 (
    .clk(clk), .in1(adder_1_out), .in2(rom_1_data), .out1(regbuf_1_out1), .out2(regbuf_1_out2),
    .WE(not_2_out), .reset(jump));  // open: in3, in4, in5, in6, out3, out4, out5, out6, in7, out7, in8, out8, in9, out9, in10, out10, in11, out11, in12, out12, in13, out13, in14, out14, in15, out15
  Comparator #(.width(32)) comparator_1 (
    .a(regbuf_1_out2), .b({32{1'b0}}), .eq(controller_1_aluy[25]));  // open: gt, lt
  Comparator #(.width(32), .mode("unsigned")) comparator_2 (
    .a(32'hc), .b(regbuf_1_out2), .eq(syscall));  // open: gt, lt
  Comparator #(.width(6)) comparator_3 (.a(6'b011000), .b(regbuf_1_out2[5:0]), .eq(comparator_3_eq));  // open: gt, lt
  Comparator #(.width(6), .mode("unsigned")) comparator_4 (
    .a(regbuf_1_out2[31:26]), .b(6'b010000), .eq(cp0));  // open: gt, lt
  Comparator #(.width(5)) comparator_5 (.a({5{1'b0}}), .b(regbuf_1_out2[25:21]), .eq(comparator_5_eq));  // open: gt, lt
  Comparator #(.width(5)) comparator_6 (.a(5'b00100), .b(regbuf_1_out2[25:21]), .eq(comparator_6_eq));  // open: gt, lt
  and and_1 (eret, comparator_3_eq, cp0);
  and and_2 (mfc0, cp0, comparator_5_eq);
  and and_3 (mtc0, cp0, comparator_6_eq);
  Multiplexer #(.width(5), .enable("false")) multiplexer_5 (
    .in0(regbuf_1_out2[20:16]), .in1(regbuf_1_out2[15:11]), .out(multiplexer_5_out), .sel(R));
  controller controller_1 (
    .op(regbuf_1_out2[31:26]), .func(regbuf_1_out2[5:0]), .R(R), .jr(controller_1_aluy[17]),
    .srav(controller_1_aluy[16]), .WE(WE), .lw(lw), .sw(controller_1_aluy[13]),
    .aluy(controller_1_aluy[5:4]), .jal(jal), .bne(controller_1_aluy[11]), .beq(controller_1_aluy[10]),
    .PCjump(controller_1_aluy[9]), .isRshift(controller_1_aluy[8]), .bltz(controller_1_aluy[7]),
    .lh(controller_1_aluy[6]), .ALUOP(controller_1_aluop));
  Multiplexer #(.width(5), .enable("false")) multiplexer_6 (
    .in0(multiplexer_5_out), .in1({5{1'b1}}), .out(multiplexer_6_out), .sel(jal));
  Multiplexer #(.width(5), .enable("false")) multiplexer_7 (
    .in0(regbuf_1_out2[25:21]), .in1(5'b00010), .out(multiplexer_7_out), .sel(syscall));
  Multiplexer #(.width(5), .enable("false")) multiplexer_8 (
    .in0(regbuf_1_out2[20:16]), .in1(5'b00100), .out(multiplexer_8_out), .sel(syscall));
  Multiplexer #(.width(32), .enable("false")) multiplexer_9 (
    .in0(multiplexer_11_out), .in1({adder_1_out[31:28], regbuf_2_out2[25:0], 2'b00}),
    .out(multiplexer_9_out), .sel(regbuf_2_out3[9]));
  // CS1402_U201414615_贾文波_regfile_main main_1: pin names not known; wires that end beside it: multiplexer_7_out, multiplexer_8_out, _5RW_num[4:0], _5Res, _5WE, clk, main_1_p7, main_1_p8
  Multiplexer #(.width(32), .enable("false")) multiplexer_10 (
    .in0({{6{1'b0}}, controller_1_aluy[25], 1'b0, syscall, eret, mtc0, mfc0, cp0, R, controller_1_aluy[17:16], WE, lw, controller_1_aluy[13], jal, controller_1_aluy[11:4], controller_1_aluop}),
    .in1({32{1'b0}}), .out(multiplexer_10_out), .sel(load_use));
  Multiplexer #(.width(32), .enable("false")) multiplexer_11 (
    .in0(multiplexer_14_out), .in1(multiplexer_12_out), .out(multiplexer_11_out), .sel(regbuf_2_out3[7]));
  assign bit_extender_1_out = {{27{1'b0}}, multiplexer_7_out};  // Bit_Extender bit_extender_1
  assign bit_extender_2_out = {{27{1'b0}}, multiplexer_8_out};  // Bit_Extender bit_extender_2
  assign bit_extender_3_out = {{27{1'b0}}, multiplexer_6_out};  // Bit_Extender bit_extender_3
  Multiplexer #(.width(32), .enable("false")) multiplexer_12 (
    .in0(regbuf_2_out1), .in1(alu_1_p5), .out(multiplexer_12_out), .sel(lessthan0));
  Comparator #(.width(32)) comparator_7 (.a(redirect_1_output), .b({32{1'b0}}), .lt(lessthan0));  // open: gt, eq
  Multiplexer #(.width(32), .enable("false")) multiplexer_13 (
    .in0(bit_extender_3_out), .in1({32{1'b0}}), .out(multiplexer_13_out), .sel(load_use));
  Multiplexer #(.width(32), .enable("false")) multiplexer_14 (
    .in0(multiplexer_15_out), .in1(redirect_1_output), .out(multiplexer_14_out), .sel(regbuf_2_out3[17]));
  regBuf regbuf_2 (
    .clk(clk), .in1(regbuf_1_out1), .in2(regbuf_1_out2), .in3(multiplexer_10_out), .in4(main_1_p7),
    .in5(main_1_p8), .in6(bit_extender_1_out), .out1(regbuf_2_out1), .out2(regbuf_2_out2),
    .out3({regbuf_2_out3, ALUOP}), .out4(regbuf_2_out4), .out5(regbuf_2_out5), .out6(regbuf_2_out6),
    .in7(bit_extender_2_out), .out7(regbuf_2_out7), .in8(multiplexer_13_out), .out8(regbuf_2_out8),
    .reset(jump));  // open: in9, out9, in10, out10, in11, out11, in12, out12, in13, out13, in14, out14, in15, out15, WE
  Multiplexer #(.width(32), .enable("false")) multiplexer_15 (
    .in0(multiplexer_16_out), .in1(multiplexer_18_out), .out(multiplexer_15_out), .sel(regbuf_2_out3[10]));
  Comparator #(.width(32)) comparator_8 (
    .a(bit_extender_1_out), .b(regbuf_2_out8), .eq(comparator_8_eq));  // open: gt, lt
  Comparator #(.width(32)) comparator_9 (
    .a(bit_extender_2_out), .b(regbuf_2_out8), .eq(comparator_9_eq));  // open: gt, lt
  Multiplexer #(.width(32), .enable("false")) multiplexer_16 (
    .in0(regbuf_2_out1), .in1(multiplexer_17_out), .out(multiplexer_16_out), .sel(regbuf_2_out3[11]));
  Multiplexer #(.width(32), .enable("false")) multiplexer_17 (
    .in0(adder_2_out), .in1(regbuf_2_out1), .out(multiplexer_17_out), .sel(aluEq));
  Multiplexer #(.width(32), .enable("false")) multiplexer_18 (
    .in0(regbuf_2_out1), .in1(adder_2_out), .out(multiplexer_18_out), .sel(aluEq));
  or or_1 (or_1_out, comparator_8_eq, comparator_9_eq);
  and and_4 (load_use, or_1_out, regbuf_2_out3[14]);
  redirect redirect_1 (
    ._5WE(_5WE), .\reg (regbuf_2_out6), .regData(regbuf_2_out4), ._5Data(_5Res), ._5RW_num(_5RW_num),
    ._4Data(_4Res), ._4RW_num(_4RW_num), ._4WE(_4WE), .\output (redirect_1_output));
  redirect redirect_2 (
    ._5WE(_5WE), .\reg (regbuf_2_out7), .regData(regbuf_2_out5), ._5Data(_5Res), ._5RW_num(_5RW_num),
    ._4Data(_4Res), ._4RW_num(_4RW_num), ._4WE(_4WE), .\output (redirect_2_output));
  assign bit_extender_4_out = {{16{1'b0}}, regbuf_2_out2[15:0]};  // Bit_Extender bit_extender_4
  assign bit_extender_5_out = {{16{regbuf_2_out2[15]}}, regbuf_2_out2[15:0]};  // Bit_Extender bit_extender_5
  assign bit_extender_6_out = {{27{1'b0}}, regbuf_2_out2[10:6]};  // Bit_Extender bit_extender_6
  assign bit_extender_7_out = {{14{regbuf_2_out2[15]}}, {regbuf_2_out2[15:0], 2'b00}};  // Bit_Extender bit_extender_7
  Shifter #(.width(32)) shifter_1 (.in(bit_extender_5_out), .\dist (5'b00010), .out(shifter_1_out));
  Multiplexer #(.width(32), .enable("false")) multiplexer_19 (
    .in0(redirect_2_output), .in1(bit_extender_6_out), .out(multiplexer_19_out), .sel(regbuf_2_out3[8]));
  Adder #(.width(32)) adder_2 (.a(shifter_1_out), .b(regbuf_2_out1), .out(adder_2_out), .cin(1'b0));  // open: cout
  Multiplexer #(.width(32), .enable("false")) multiplexer_20 (
    .in0(redirect_1_output), .in1(redirect_2_output), .out(multiplexer_20_out), .sel(regbuf_2_out3[8]));
  Multiplexer #(.select(2), .width(32), .enable("false")) multiplexer_21 (
    .in0(bit_extender_4_out), .in1(bit_extender_5_out), .in2(redirect_2_output), .in3(bit_extender_7_out),
    .out(multiplexer_21_out), .sel(regbuf_2_out3[5:4]));
  Multiplexer #(.width(32), .enable("false")) multiplexer_22 (
    .in0(multiplexer_19_out), .in1(redirect_1_output), .out(multiplexer_22_out), .sel(regbuf_2_out3[16]));
  Multiplexer #(.width(32), .enable("false")) multiplexer_23 (
    .in0(multiplexer_20_out), .in1(regbuf_2_out1), .out(multiplexer_23_out), .sel(regbuf_2_out3[7]));
  Multiplexer #(.width(32), .enable("false")) multiplexer_24 (
    .in0(multiplexer_21_out), .in1(multiplexer_22_out), .out(multiplexer_24_out), .sel(regbuf_2_out3[18]));
  Multiplexer #(.width(32), .enable("false")) multiplexer_25 (
    .in0(multiplexer_26_out), .in1(cp0Data), .sel(mfc0));  // open: out
  Multiplexer #(.width(32), .enable("false")) multiplexer_26 (
    .in0(undriven), .in1(PC), .out(multiplexer_26_out), .sel(jal));
  not not_3 (not_3_out, aluEq);
  // ALU alu_1: pin names not known; wires that end beside it: multiplexer_23_out, multiplexer_24_out, ALUOP, aluEq, alu_1_p5
  or or_2 (uncondjump, regbuf_2_out3[17], regbuf_2_out3[9]);
  and and_5 (and_5_out, regbuf_2_out3[10], aluEq);
  and and_6 (and_6_out, regbuf_2_out3[11], not_3_out);
  and and_7 (and_7_out, regbuf_2_out3[7], lessthan0);
  or or_3 (condjump, and_5_out, and_6_out, and_7_out);
  or or_4 (jump, uncondjump, condjump);
  regBuf regbuf_3 (
    .clk(clk), .in1(regbuf_2_out1), .in2({regbuf_2_out3, ALUOP}), .in3(alu_1_p5), .in4(redirect_2_output),
    .in5(regbuf_2_out8), .in6(redirect_1_output), .out1(regbuf_3_out1),
    .out2({regbuf_3_out2[31:16], _4WE, regbuf_3_out2[14:0]}), .out3(_4Res), .out4(regbuf_3_out4),
    .out5(_4RW_num), .out6(regbuf_3_out6), .reset(1'b0));  // open: in7, out7, in8, out8, in9, out9, in10, out10, in11, out11, in12, out12, in13, out13, in14, out14, in15, out15, WE
  and and_8 (and_8_out, ~regbuf_3_out2[25], ~regbuf_3_out2[23], regbuf_3_out2[13]);  // AND_Gate
  RAM #(.addrWidth(24), .dataWidth(32), .bus("separate")) ram_1 (
    .addr(_4Res[25:2]), .din(regbuf_3_out4), .data(ram_1_data), .str(and_8_out), .clk(clk), .ld(1'b1),
    .clr(1'b0));  // open: sel
  Multiplexer #(.width(32), .enable("false")) multiplexer_27 (
    .in0(multiplexer_28_out), .in1(regbuf_4_out1), .out(_5Res), .sel(regbuf_4_out2[12]));
  regBuf regbuf_4 (
    .clk(clk), .in1(regbuf_3_out1), .in2({regbuf_3_out2[31:16], _4WE, regbuf_3_out2[14:0]}),
    .in3(ram_1_data), .in4(_4Res), .in5(regbuf_3_out4), .in6(_4RW_num), .out1(regbuf_4_out1),
    .out2(regbuf_4_out2), .out3(regbuf_4_out3), .out4(regbuf_4_out4), .out5(regbuf_4_out5), .out6(_5RW_num),
    .in7(regbuf_3_out6), .out7(regbuf_4_out7), .reset(1'b0));  // open: in8, out8, in9, out9, in10, out10, in11, out11, in12, out12, in13, out13, in14, out14, in15, out15, WE
  and and_9 (_5WE, or_5_out, ~regbuf_4_out2[23], ~regbuf_4_out2[25]);  // AND_Gate
  or or_5 (or_5_out, regbuf_4_out2[20], regbuf_4_out2[15]);
  Multiplexer #(.width(32), .enable("false")) multiplexer_28 (
    .in0(multiplexer_30_out), .in1(regbuf_4_out3), .out(multiplexer_28_out), .sel(regbuf_4_out2[14]));
  Comparator #(.width(32)) comparator_10 (.a(regbuf_4_out7), .b(32'ha), .eq(comparator_10_eq));  // open: gt, lt
  Hex_Digit_Display hex_digit_display_1 (.value(register_3_q_8));  // open: dp
  Multiplexer #(.width(16), .enable("false")) multiplexer_29 (
    .in0(regbuf_4_out3[15:0]), .in1(regbuf_4_out3[31:16]), .out(multiplexer_29_out), .sel(regbuf_4_out4[1]));
  assign bit_extender_8_out = {{16{multiplexer_29_out[15]}}, multiplexer_29_out};  // Bit_Extender bit_extender_8
  Multiplexer #(.width(32), .enable("false")) multiplexer_30 (
    .in0(regbuf_4_out4), .in1(bit_extender_8_out), .out(multiplexer_30_out), .sel(regbuf_4_out2[6]));
  and and_10 (and_10_out, comparator_10_eq, regbuf_4_out2[23]);
  Clock clock_1 (.out(clock_1_out));
  Hex_Digit_Display hex_digit_display_2 (.value(register_3_q_7));  // open: dp
  Hex_Digit_Display hex_digit_display_3 (.value(register_3_q_6));  // open: dp
  not not_4 (not_4_out, and_10_out);
  Multiplexer #(.enable("false")) multiplexer_31 (.in0(clock_1_out), .in1(1'b0), .out(clk), .sel(register_2_q));
  Register #(.width(1)) register_2 (.D(and_10_out), .Q(register_2_q), .clk(clk));  // open: en, clr
  Hex_Digit_Display hex_digit_display_4 (.value(register_3_q_4));  // open: dp
  Hex_Digit_Display hex_digit_display_5 (.value(register_3_q_5));  // open: dp
  and and_11 (and_11_out, not_4_out, regbuf_4_out2[23]);
  Counter #(.width(32), .max('hffffffff)) counter_1 (
    .count(1'b1), .Q(counter_1_q), .clk(clk));  // open: load, D, carry, clr
  // Probe on counter_1_q
  Hex_Digit_Display hex_digit_display_6 (.value(register_3_q_2));  // open: dp
  Hex_Digit_Display hex_digit_display_7 (.value(register_3_q_3));  // open: dp
  Register #(.width(32)) register_3 (
    .D(regbuf_4_out5), .en(and_11_out),
    .Q({register_3_q_8, register_3_q_7, register_3_q_6, register_3_q_5, register_3_q_4, register_3_q_3, register_3_q_2, register_3_q}),
    .clk(clk));  // open: clr
  Counter #(.width(32), .max('hffffffff)) counter_2 (
    .load(1'b0), .D(counter_2_q), .count(load_use), .Q(counter_2_q), .clk(clk));  // open: carry, clr
  Hex_Digit_Display hex_digit_display_8 (.value(register_3_q));  // open: dp
  // Probe on counter_2_q
  Counter #(.width(32), .max('hffffffff)) counter_3 (
    .load(1'b0), .D(counter_3_q), .count(regbuf_4_out2[23]), .Q(counter_3_q), .clk(clk));  // open: carry, clr
  // Probe on counter_3_q
  // Probe on counter_4_q
  Counter #(.width(32), .max('hffffffff)) counter_4 (
    .load(1'b0), .D(counter_4_q), .count(uncondjump), .Q(counter_4_q), .clk(clk));  // open: carry, clr
  // Probe on counter_5_q
  Counter #(.width(32), .max('hffffffff)) counter_5 (
    .load(1'b0), .D(counter_5_q), .count(condjump), .Q(counter_5_q), .clk(clk));  // open: carry, clr
  // Probe on adder_4_out
  Adder #(.width(32)) adder_3 (.a(counter_5_q), .b(counter_4_q), .out(adder_3_out));  // open: cin, cout
  Shifter #(.width(32)) shifter_2 (.in(adder_3_out), .\dist (5'b00001), .out(shifter_2_out));
  Adder #(.width(32)) adder_4 (.a(shifter_2_out), .b(counter_2_q), .out(adder_4_out));  // open: cin, cout

  // Notes on the sheet:
  //   排除掉eret的情况，否则有中断等待时会卡死
  //   contents of rom_1 (hex, n*v repeats v):
  //   2010ffff 20110000 ae300000 22100001 22310004 ae300000 22100001 22310004 ae300000 22100001 22310004
  //   ae300000 22100001 22310004 ae300000 22100001 22310004 ae300000 22100001 22310004 ae300000 22100001
  //   22310004 ae300000 22100001 22310004 ae300000 22100001 22310004 ae300000 22100001 22310004 ae300000
  //   22100001 22310004 ae300000 22100001 22310004 ae300000 22100001 22310004 ae300000 22100001 22310004
  //   ae300000 22100001 22310004 ae300000 22100001 22310004 22100001 8020 2011003c 8e130000 8e340000
  //   274402a 11000002 ae330000 ae140000 2231fffc 1611fff8 102020 20020022 c 22100004 2011003c 1611fff2
  //   2002000a c
  //   R1
  //   R2
  //   bne
  //   beq
  //   R2
  //   无条件跳转，j、jal、jr
  //   这里的reset需要接0
  //   忘记接jal
  //   R1
  //   R2
  //   alu
  //   mem
  //   周期数
  //   load-use冲突数
  //   syscall次数
  //   无条件跳转次数
  //   有条件成功跳转次数
  //   气泡数
endmodule

module controller (
  input  [5:0] op,
  input  [5:0] func,
  output lw,
  output sw,
  output jal,
  output bne,
  output beq,
  output PCjump,
  output bltz,
  output lh,
  output R,
  output WE,
  output jr,
  output isRshift,
  output [1:0] aluy,
  output srav,
  output [3:0] ALUOP
);

  wire and_2_out, j, nor_2_out, not_1_out, not_2_out, not_3_out, not_4_out, not_5_out;
  wire [3:0] opi_1_alu0, opr_1_alu0;

  nor nor_1 (R, op[5], op[4], op[3], op[2], op[1], op[0]);
  opi opi_1 (
    .op5(op[5]), .op4(op[4]), .op3(op[3]), .op2(op[2]), .op1(op[1]), .op0(op[0]), .alu3(opi_1_alu0[3]),
    .alu2(opi_1_alu0[2]), .alu1(opi_1_alu0[1]), .alu0(opi_1_alu0[0]));
  opr opr_1 (
    .func5(func[5]), .func4(func[4]), .func3(func[3]), .func2(func[2]), .func1(func[1]), .func0(func[0]),
    .alu3(opr_1_alu0[3]), .alu2(opr_1_alu0[2]), .alu1(opr_1_alu0[1]), .alu0(opr_1_alu0[0]));
  not not_1 (not_1_out, func[3]);
  nor nor_2 (nor_2_out, func[5], func[4], not_1_out, func[2], func[1], func[0]);
  and and_1 (jr, nor_2_out, R);
  Multiplexer #(.width(4), .enable("false")) multiplexer_1 (.in0(opi_1_alu0), .in1(opr_1_alu0), .out(ALUOP), .sel(R));
  inst inst_1 (
    .p5(op[5]), .p4(op[4]), .p3(op[3]), .p2(op[2]), .p1(op[1]), .p0(op[0]), .jal(jal), .lw(lw), .sw(sw),
    .beq(beq), .bne(bne), .j(j), .lh(lh), .bltz(bltz));
  not not_2 (not_2_out, func[4]);
  not not_3 (not_3_out, func[5]);
  nor nor_3 (WE, bltz, jr, j, bne, beq, sw);
  not not_4 (not_4_out, func[3]);
  and and_2 (and_2_out, not_3_out, not_2_out, not_4_out, func[2], func[1], func[0]);
  and and_3 (srav, and_2_out, R);
  aluy aluy_1 (.p5(op[5]), .p4(op[4]), .p3(op[3]), .p2(op[2]), .p1(op[1]), .p0(op[0]), .b1(aluy[1]), .b0(aluy[0]));
  or or_1 (PCjump, j, jal);
  not not_5 (not_5_out, func[5]);
  and and_4 (isRshift, not_5_out, R);

  // Other names for the same wires on the sheet: F0 = func[0]; F1 = func[1]; F2 = func[2]; F3 = func[3]; F4 = func[4];
  //   F5 = func[5]; P0 = op[0]; P1 = op[1]; P2 = op[2]; P3 = op[3]; P4 = op[4]; P5 = op[5]

  // Notes on the sheet:
  //   0：无符号扩展，1：符号扩展，2：RF.R2，3：bltz
endmodule

module opi (
  input  op5,
  input  op4,
  input  op3,
  input  op2,
  input  op1,
  input  op0,
  output alu3,
  output alu2,
  output alu1,
  output alu0
);

  wire and_1_out, and_2_out, and_3_out, and_4_out, and_5_out, and_6_out, and_7_out, and_8_out, not_1_out,
       not_2_out, not_3_out, not_4_out, not_5_out, not_6_out, not_7_out, not_8_out, not_9_out, not_10_out,
       not_11_out, not_12_out, not_13_out, not_14_out;

  not not_1 (not_1_out, op3);
  not not_2 (not_2_out, op0);
  not not_3 (not_3_out, op0);
  not not_4 (not_4_out, op2);
  not not_5 (not_5_out, op1);
  not not_6 (not_6_out, op0);
  not not_7 (not_7_out, op2);
  not not_8 (not_8_out, op0);
  not not_9 (not_9_out, op3);
  not not_10 (not_10_out, op1);
  not not_11 (not_11_out, op0);
  not not_12 (not_12_out, op3);
  not not_13 (not_13_out, op2);
  not not_14 (not_14_out, op0);
  and and_1 (and_1_out, not_1_out, not_2_out);
  and and_2 (and_2_out, op1, not_3_out);
  and and_3 (and_3_out, op2, op0);
  and and_4 (and_4_out, not_4_out, op0);
  and and_5 (and_5_out, op3, not_5_out, not_6_out);
  and and_6 (and_6_out, not_7_out, op1, not_8_out);
  and and_7 (and_7_out, not_9_out, op2);
  and and_8 (and_8_out, op2, not_10_out, not_11_out);
  or or_1 (alu0, not_12_out, not_13_out, not_14_out);
  or or_2 (alu3, and_1_out, and_2_out, and_3_out);
  or or_3 (alu2, and_4_out, and_5_out);
  or or_4 (alu1, and_6_out, and_7_out, and_8_out);
endmodule

module opr (
  input  func5,
  input  func4,
  input  func3,
  input  func2,
  input  func1,
  input  func0,
  output alu3,
  output alu2,
  output alu1,
  output alu0
);

  wire and_1_out, and_2_out, and_3_out, and_4_out, and_5_out, and_6_out, and_7_out, and_8_out, and_9_out,
       and_10_out, and_11_out, not_1_out, not_2_out, not_3_out, not_4_out, not_5_out, not_6_out, not_7_out,
       not_8_out, not_9_out, not_10_out, not_11_out;

  and and_1 (and_1_out, func5, func2, func0);
  not not_1 (not_1_out, func0);
  not not_2 (not_2_out, func3);
  not not_3 (not_3_out, func2);
  not not_4 (not_4_out, func0);
  not not_5 (not_5_out, func0);
  not not_6 (not_6_out, func3);
  not not_7 (not_7_out, func5);
  not not_8 (not_8_out, func0);
  not not_9 (not_9_out, func0);
  not not_10 (not_10_out, func2);
  not not_11 (not_11_out, func1);
  or or_1 (alu3, func3, and_1_out);
  and and_2 (and_2_out, func2, not_1_out);
  and and_3 (and_3_out, func3, func0);
  and and_4 (and_4_out, func5, not_2_out, not_3_out);
  and and_5 (and_5_out, func1, not_4_out);
  and and_6 (and_6_out, func2, not_5_out);
  and and_7 (and_7_out, func5, not_6_out, func1);
  and and_8 (and_8_out, not_7_out, func0);
  and and_9 (and_9_out, func2, not_8_out);
  and and_10 (and_10_out, func3, not_9_out);
  and and_11 (and_11_out, func5, not_10_out, not_11_out);
  or or_2 (alu2, and_2_out, and_3_out, and_4_out);
  or or_3 (alu1, and_5_out, and_6_out, and_7_out);
  or or_4 (alu0, and_8_out, and_9_out, and_10_out, and_11_out);
endmodule

module inst (
  input  p5,
  input  p4,
  input  p3,
  input  p2,
  input  p1,
  input  p0,
  output jal,
  output lw,
  output sw,
  output beq,
  output bne,
  output j,
  output lh,
  output bltz
);

  wire and_3_out, and_4_out, and_5_out, and_6_out, and_8_out, and_9_out, not_1_out, not_2_out, not_3_out,
       not_4_out, not_5_out, not_6_out, not_7_out, not_8_out, not_9_out, not_10_out, not_11_out, not_12_out,
       not_13_out, not_14_out, not_15_out, not_16_out, not_17_out, not_18_out, not_19_out;

  not not_1 (not_1_out, p5);
  not not_2 (not_2_out, p3);
  not not_3 (not_3_out, p0);
  not not_4 (not_4_out, p3);
  not not_5 (not_5_out, p3);
  not not_6 (not_6_out, p3);
  and and_1 (sw, p5, p3);
  not not_7 (not_7_out, p3);
  not not_8 (not_8_out, p0);
  not not_9 (not_9_out, p3);
  not not_10 (not_10_out, p1);
  not not_11 (not_11_out, p3);
  not not_12 (not_12_out, p1);
  not not_13 (not_13_out, p3);
  not not_14 (not_14_out, p0);
  not not_15 (not_15_out, p1);
  not not_16 (not_16_out, p5);
  not not_17 (not_17_out, p3);
  not not_18 (not_18_out, p2);
  not not_19 (not_19_out, p1);
  and and_2 (jal, not_1_out, p1, p0);
  and and_3 (and_3_out, p5, not_2_out, not_3_out);
  and and_4 (and_4_out, p5, not_4_out, p1);
  and and_5 (and_5_out, p5, not_5_out, p2);
  and and_6 (and_6_out, p5, p4, not_6_out);
  and and_7 (beq, not_7_out, p2, not_8_out);
  and and_8 (and_8_out, not_9_out, p2, not_10_out, p0);
  and and_9 (and_9_out, p4, not_11_out, not_12_out, p0);
  and and_10 (j, not_13_out, p1, not_14_out);
  and and_11 (lh, p5, not_15_out);
  and and_12 (bltz, not_16_out, not_17_out, not_18_out, not_19_out, p0);
  or or_1 (lw, and_3_out, and_4_out, and_5_out, and_6_out);
  or or_2 (bne, and_8_out, and_9_out);
endmodule

module aluy (
  input  p5,
  input  p4,
  input  p3,
  input  p2,
  input  p1,
  input  p0,
  output b1,
  output b0
);

  wire and_2_out, and_3_out, not_1_out, not_2_out, not_3_out, not_4_out, not_5_out, not_6_out;

  not not_1 (not_1_out, p5);
  not not_2 (not_2_out, p3);
  not not_3 (not_3_out, p3);
  not not_4 (not_4_out, p2);
  not not_5 (not_5_out, p2);
  not not_6 (not_6_out, p0);
  and and_1 (b1, not_1_out, not_2_out);
  and and_2 (and_2_out, not_3_out, not_4_out);
  and and_3 (and_3_out, not_5_out, not_6_out);
  or or_1 (b0, and_2_out, and_3_out, p5);
endmodule

module interrupt (
  input  int1,
  input  int2,
  input  eret,
  input  int3,
  input  WE,
  input  [31:0] in,
  input  [4:0] w_num,
  input  [4:0] R_num,
  input  clk,
  output \break ,
  output select,
  output [31:0] address,
  output _1wait,
  output _2wait,
  output _3wait,
  output [31:0] out
);

  wire and_1_out, and_2_out, and_3_out, and_4_out, and_5_out, and_6_out, and_7_out, and_8_out,
       decoder_1_out0, decoder_1_out1, decoder_2_out1, decoder_2_out2, decoder_2_out3, IR1_q, IR2_q, IR3_q,
       multiplexer_1_out, multiplexer_2_out, multiplexer_3_out, nand_1_out, nor_1_out, not_1_out, not_2_out,
       or_1_out, or_2_out, or_3_out, or_4_out;
  wire [1:0] multiplexer_5_out, priority_encoder_1_out;
  wire [31:0] EPC_q, IE_q, multiplexer_4_out;

  D_Flip_Flop d_ff_1 (.clk(int1), .D(1'b1), .Q(_1wait), .reset(and_1_out));  // open: Qn, preset, en
  D_Flip_Flop d_ff_2 (.clk(int2), .D(1'b1), .Q(_2wait), .reset(and_2_out));  // open: Qn, preset, en
  D_Flip_Flop d_ff_3 (.clk(int3), .D(1'b1), .Q(_3wait), .reset(and_3_out));  // open: Qn, preset, en
  Decoder #(.enable("false")) decoder_1 (.out0(decoder_1_out0), .out1(decoder_1_out1), .sel(w_num[0]));
  Multiplexer #(.enable("false")) multiplexer_1 (.in0(_1wait), .in1(1'b0), .out(multiplexer_1_out), .sel(and_1_out));
  Multiplexer #(.enable("false")) multiplexer_2 (.in0(_2wait), .in1(1'b0), .out(multiplexer_2_out), .sel(and_2_out));
  Multiplexer #(.enable("false")) multiplexer_3 (.in0(_3wait), .in1(1'b0), .out(multiplexer_3_out), .sel(and_3_out));
  Multiplexer #(.width(32), .enable("false")) multiplexer_4 (
    .in0(in), .in1(32'h1), .out(multiplexer_4_out), .sel(\break ));
  D_Flip_Flop IR1 (.clk(clk), .D(multiplexer_1_out), .Q(IR1_q));  // open: Qn, preset, en, reset
  D_Flip_Flop IR2 (.clk(clk), .D(multiplexer_2_out), .Q(IR2_q));  // open: Qn, preset, en, reset
  D_Flip_Flop IR3 (.clk(clk), .D(multiplexer_3_out), .Q(IR3_q));  // open: Qn, preset, en, reset
  and and_1 (and_1_out, decoder_2_out1, \break , IE_q[0]);
  and and_2 (and_2_out, decoder_2_out2, \break , IE_q[0]);
  and and_3 (and_3_out, decoder_2_out3, \break , IE_q[0]);
  and and_4 (and_4_out, WE, decoder_1_out0);
  and and_5 (and_5_out, WE, decoder_1_out1);
  nor nor_1 (nor_1_out, address[8], address[9]);
  not not_1 (not_1_out, address[9]);
  and and_6 (and_6_out, IR1_q, nor_1_out, ~IE_q[0]);  // AND_Gate
  and and_7 (and_7_out, IR2_q, not_1_out, ~IE_q[0]);  // AND_Gate
  and and_8 (and_8_out, IR3_q, nand_1_out, ~IE_q[0]);  // AND_Gate
  nand nand_1 (nand_1_out, address[9], address[8]);
  or or_1 (or_1_out, and_4_out, \break );
  or or_2 (or_2_out, and_5_out, \break );
  Register #(.width(32)) IE (.D(multiplexer_4_out), .en(or_1_out), .Q(IE_q), .clk(clk));  // open: clr
  Register #(.width(32)) EPC (.D(in), .en(or_2_out), .Q(EPC_q), .clk(clk));  // open: clr
  Priority_Encoder #(.select(2)) priority_encoder_1 (
    .in0(1'b0), .in1(and_6_out), .in2(and_7_out), .in3(and_8_out), .out(priority_encoder_1_out), .gs(\break ));  // open: en_out, en_in
  Decoder #(.select(2), .enable("false")) decoder_2 (
    .out1(decoder_2_out1), .out2(decoder_2_out2), .out3(decoder_2_out3), .sel(address[9:8]));  // open: out0
  Multiplexer #(.width(2), .enable("false")) multiplexer_5 (
    .in0(2'b00), .in1(priority_encoder_1_out), .out(multiplexer_5_out), .sel(\break ));
  or or_3 (or_3_out, \break , eret);
  shiftReg shiftreg_1 (.direct(eret), .WE(or_3_out), .data(multiplexer_5_out), .clk(clk), .\output (address[9:8]));
  Multiplexer #(.width(32), .enable("false")) multiplexer_6 (.in0(IE_q), .in1(EPC_q), .out(out), .sel(or_4_out));
  or or_4 (or_4_out, eret, R_num[0]);
  D_Flip_Flop #(.trigger("falling")) d_ff_4 (
    .clk(\break ), .D(1'b1), .Q(select), .reset(not_2_out));  // open: Qn, preset, en
  not not_2 (not_2_out, clk);

  assign {address[31:10], address[7:0]} = 30'h300;

  // Other names for the same wires on the sheet: cp = clk; hasInt = \break 

  // Notes on the sheet:
  //   hasInt时in传入pc
  //   优先级：中断1<2<3
  //   隐指令关中断的时候清零，排除指令关中断的情况
  //   0:IE, 1:EPC
  //   IE:0开中断，1关中断
  //   时钟下降沿清零，不能在eret时清零
endmodule

module shiftReg (
  input  direct,
  input  WE,
  input  [1:0] data,
  input  clk,
  output [1:0] \output 
);

  wire [1:0] shift_register_1_q1, shift_register_1_q2, shift_register_1_q3;

  Shift_Register #(.width(2), .length(4)) shift_register_1 (
    .shift(WE), .in(data), .clk(clk), .load(direct), .d0(shift_register_1_q1), .q0(\output ),
    .d1(shift_register_1_q2), .q1(shift_register_1_q1), .d2(shift_register_1_q3), .q2(shift_register_1_q2),
    .d3(2'b00), .q3(shift_register_1_q3));  // open: out, clr
endmodule

module regBuf (
  input  reset,
  input  WE,
  input  clk,
  input  [31:0] in1,
  input  [31:0] in2,
  input  [31:0] in3,
  input  [31:0] in4,
  input  [31:0] in5,
  input  [31:0] in6,
  input  [31:0] in7,
  input  [31:0] in8,
  input  [31:0] in9,
  input  [31:0] in10,
  input  [31:0] in11,
  input  [31:0] in12,
  input  [31:0] in13,
  input  [31:0] in14,
  input  [31:0] in15,
  output [31:0] out1,
  output [31:0] out2,
  output [31:0] out3,
  output [31:0] out4,
  output [31:0] out5,
  output [31:0] out6,
  output [31:0] out7,
  output [31:0] out8,
  output [31:0] out9,
  output [31:0] out10,
  output [31:0] out11,
  output [31:0] out12,
  output [31:0] out13,
  output [31:0] out14,
  output [31:0] out15
);

  wire not_1_out;
  wire [31:0] and_1_out, and_2_out, and_3_out, and_4_out, and_5_out, and_6_out, and_7_out, and_8_out,
       and_9_out, and_10_out, and_11_out, and_12_out, and_13_out, and_14_out, and_15_out, bit_extender_1_out;

  not not_1 (not_1_out, reset);
  assign bit_extender_1_out = {{31{not_1_out}}, not_1_out};  // Bit_Extender bit_extender_1
  assign and_1_out = bit_extender_1_out & in1;  // AND_Gate and_1, 32 bits wide
  assign and_2_out = bit_extender_1_out & in2;  // AND_Gate and_2, 32 bits wide
  assign and_3_out = bit_extender_1_out & in3;  // AND_Gate and_3, 32 bits wide
  assign and_4_out = bit_extender_1_out & in4;  // AND_Gate and_4, 32 bits wide
  assign and_5_out = bit_extender_1_out & in5;  // AND_Gate and_5, 32 bits wide
  assign and_6_out = bit_extender_1_out & in6;  // AND_Gate and_6, 32 bits wide
  assign and_7_out = bit_extender_1_out & in7;  // AND_Gate and_7, 32 bits wide
  assign and_8_out = bit_extender_1_out & in8;  // AND_Gate and_8, 32 bits wide
  assign and_9_out = bit_extender_1_out & in9;  // AND_Gate and_9, 32 bits wide
  assign and_10_out = bit_extender_1_out & in10;  // AND_Gate and_10, 32 bits wide
  assign and_11_out = bit_extender_1_out & in11;  // AND_Gate and_11, 32 bits wide
  assign and_12_out = bit_extender_1_out & in12;  // AND_Gate and_12, 32 bits wide
  assign and_13_out = bit_extender_1_out & in13;  // AND_Gate and_13, 32 bits wide
  assign and_14_out = bit_extender_1_out & in14;  // AND_Gate and_14, 32 bits wide
  assign and_15_out = bit_extender_1_out & in15;  // AND_Gate and_15, 32 bits wide
  Register #(.width(32)) register_1 (.D(and_1_out), .en(WE), .Q(out1), .clk(clk));  // open: clr
  Register #(.width(32)) register_2 (.D(and_2_out), .en(WE), .Q(out2), .clk(clk));  // open: clr
  Register #(.width(32)) register_3 (.D(and_3_out), .en(WE), .Q(out3), .clk(clk));  // open: clr
  Register #(.width(32)) register_4 (.D(and_4_out), .en(WE), .Q(out4), .clk(clk));  // open: clr
  Register #(.width(32)) register_5 (.D(and_5_out), .en(WE), .Q(out5), .clk(clk));  // open: clr
  Register #(.width(32)) register_6 (.D(and_6_out), .en(WE), .Q(out6), .clk(clk));  // open: clr
  Register #(.width(32)) register_7 (.D(and_7_out), .en(WE), .Q(out7), .clk(clk));  // open: clr
  Register #(.width(32)) register_8 (.D(and_8_out), .en(WE), .Q(out8), .clk(clk));  // open: clr
  Register #(.width(32)) register_9 (.D(and_9_out), .en(WE), .Q(out9), .clk(clk));  // open: clr
  Register #(.width(32)) register_10 (.D(and_10_out), .en(WE), .Q(out10), .clk(clk));  // open: clr
  Register #(.width(32)) register_11 (.D(and_11_out), .en(WE), .Q(out11), .clk(clk));  // open: clr
  Register #(.width(32)) register_12 (.D(and_12_out), .en(WE), .Q(out12), .clk(clk));  // open: clr
  Register #(.width(32)) register_13 (.D(and_13_out), .en(WE), .Q(out13), .clk(clk));  // open: clr
  Register #(.width(32)) register_14 (.D(and_14_out), .en(WE), .Q(out14), .clk(clk));  // open: clr
  Register #(.width(32)) register_15 (.D(and_15_out), .en(WE), .Q(out15), .clk(clk));  // open: clr
endmodule

module redirect (
  input  _5WE,
  input  [31:0] \reg ,
  input  [31:0] regData,
  input  [31:0] _5Data,
  input  [31:0] _5RW_num,
  input  [31:0] _4Data,
  input  [31:0] _4RW_num,
  input  _4WE,
  output [31:0] \output 
);

  wire and_1_out, and_2_out, comparator_1_eq, comparator_2_eq;
  wire [31:0] multiplexer_1_out;

  Multiplexer #(.width(32), .enable("false")) multiplexer_1 (
    .in0(regData), .in1(_5Data), .out(multiplexer_1_out), .sel(and_1_out));
  and and_1 (and_1_out, _5WE, comparator_1_eq);
  Comparator #(.width(5), .mode("unsigned")) comparator_1 (
    .a(\reg [4:0]), .b(_5RW_num[4:0]), .eq(comparator_1_eq));  // open: gt, lt
  Comparator #(.width(5), .mode("unsigned")) comparator_2 (
    .a(\reg [4:0]), .b(_4RW_num[4:0]), .eq(comparator_2_eq));  // open: gt, lt
  and and_2 (and_2_out, comparator_2_eq, _4WE);
  Multiplexer #(.width(32), .enable("false")) multiplexer_2 (
    .in0(multiplexer_1_out), .in1(_4Data), .out(\output ), .sel(and_2_out));
endmodule
